# Fritzing sketch pcb (saved by Fritzing 1.0.5)
breadboards: 2

parts:
  Mod1 = Raspberry Pi 4B
  U1 = SWITCH_SPDT [package=kps-1290]
  Mod2 = Raspberry Pi 4B
  LED1 = smd LED [color="Green (560nm)" package="1206 [SMD]"]
  R1 = Resistor [tolerance=±5% resistance=330 package="0402 [SMD]"]

nets:
  N1: Mod1.GND, U1.P
  N2: Mod1.GPIO23, U1.S
  N3: Mod2.GND, R1.Pin_1
  N4: Mod2.GPIO23, LED1.cathode
  N5: LED1.anode, R1.Pin_0

notes:
  Light
  Switch
